# Fritzing sketch Manifold (saved by Fritzing 1.0.6)
breadboards: 1

parts:
  A1 = ESP32-S3 zero
  Adafruit_757_Level_Shifter = Logic Level Converter [package="Breakout board"]
  230V_AC_input = screw terminal, 3 pins
  R1 = Resistor [tolerance=±5% power=0.25W resistance=330 package=THT]
  R2 = Resistor [tolerance=±5% power=0.25W resistance=330 package=THT]
  10A_Blade_Fuse = FUSE [package=fuse_5mm]
  10A_Blade_Fuse1 = FUSE [package=fuse_5mm]
  10A_Blade_Fuse2 = FUSE [package=fuse_5mm]
  10A_Blade_Fuse3 = FUSE [package=fuse_5mm]
  +V = Camdenboss CTB0158-5 [part_number=CTB0158-5 package=THT]
  -V = Camdenboss CTB0158-5 [part_number=CTB0158-5 package=THT]
  60ppm_LED_Strip_2 = WS2812 RGB LED strip
  60ppm_LED_Strip_1 = WS2812 RGB LED strip
  60ppm_LED_Strip_3 = WS2812 RGB LED strip
  60ppm_LED_Strip_4 = WS2812 RGB LED strip
  C1 = Capacitor Polarized [package=cpol-radial-1000uf-63v]
  C2 = Capacitor Polarized [package=cpol-radial-1000uf-63v]
  C3 = Capacitor Polarized [package=cpol-radial-1000uf-63v]
  C4 = Capacitor Polarized [package=cpol-radial-1000uf-63v]
  1A_Fuse = FUSE [package=fuse_5mm]

nets (from the schematic view):
  N1: A1.Pin_1, 1A_Fuse.2
  N2: A1.Pin_2, Adafruit_757_Level_Shifter.L-GND, Adafruit_757_Level_Shifter.H-GND, -V.terminal_1
  N3: A1.Pin_3, Adafruit_757_Level_Shifter.LV
  N4: A1.Pin_4, Adafruit_757_Level_Shifter.LV1
  N5: A1.Pin_5, Adafruit_757_Level_Shifter.LV2
  N6: Adafruit_757_Level_Shifter.HV, +V.terminal_1, 1A_Fuse.1
  N7: Adafruit_757_Level_Shifter.HV2, R2.Pin_1
  N8: Adafruit_757_Level_Shifter.HV1, R1.Pin_1
  GND: 230V_AC_input.pin1
  N9: 230V_AC_input.pin2, -V.pin1, -V.pin2, -V.pin3, -V.pin4, -V.pin5
  N10: 230V_AC_input.pin3, +V.pin1, +V.pin2, +V.pin3, +V.pin4, +V.pin5
  N11: R1.Pin_0, 60ppm_LED_Strip_2.DIN
  N12: R2.Pin_0, 60ppm_LED_Strip_3.DIN
  N13: 10A_Blade_Fuse.1, +V.terminal_2
  N14: 10A_Blade_Fuse.2, 60ppm_LED_Strip_3.VCC#1, C3.+
  N15: 10A_Blade_Fuse1.1, +V.terminal_3
  N16: 10A_Blade_Fuse1.2, 60ppm_LED_Strip_4.VCC#5, C4.+
  N17: 10A_Blade_Fuse2.1, +V.terminal_4
  N18: 10A_Blade_Fuse2.2, 60ppm_LED_Strip_2.VCC#1, C1.+
  N19: 10A_Blade_Fuse3.1, +V.terminal_5
  N20: 10A_Blade_Fuse3.2, 60ppm_LED_Strip_1.VCC#5, C2.+
  N21: -V.terminal_2, 60ppm_LED_Strip_3.GND#0, C3.-
  N22: -V.terminal_3, 60ppm_LED_Strip_4.GND#4, C4.-
  N23: -V.terminal_4, 60ppm_LED_Strip_2.GND#0, C1.-
  N24: -V.terminal_5, 60ppm_LED_Strip_1.GND#4, C2.-
  N25: 60ppm_LED_Strip_2.GND#4, 60ppm_LED_Strip_1.GND#0
  N26: 60ppm_LED_Strip_2.VCC#5, 60ppm_LED_Strip_1.VCC#1
  N27: 60ppm_LED_Strip_2.DOUT, 60ppm_LED_Strip_1.DIN
  N28: 60ppm_LED_Strip_3.GND#4, 60ppm_LED_Strip_4.GND#0
  N29: 60ppm_LED_Strip_3.VCC#5, 60ppm_LED_Strip_4.VCC#1
  N30: 60ppm_LED_Strip_3.DOUT, 60ppm_LED_Strip_4.DIN

notes:
  5V 60A Industrial PSU (300W)
  The system utilizes a 300W PSU but is software-governed to 150W (30A). Each 5m segment is individually fused at 10A to protect the 1.0mm² cabling and the LED strip traces from overcurrent. A common ground bus is maintained throughout to ensure signal integrity and prevent ground loops.
  LED Strips: 4x 5m WS2812B (60 LEDs/m). Total: 1,200 Pixels. Each pixel max 60mA at full white, full brightness. Typical RGB load is 20mA.
  Current Limit (Software): WLED Software Power Limiter set to 30A max current draw for system.
  Data Flow: Output Pin 1: 600 LEDs (Strips 1 & 2), Reversed in software. Output Pin 2: 600 LEDs (Strips 3 & 4).
  Shielding: 50mm minimum clearance between the 5V DC power cables and the Data signal wires on LED strips to prevent Electromagnetic Interference.
  Main Power Supply: 5V DC, 60A (300W). Input AC voltage 230V AC grounded (earthed) AC plug.
  Fuses: Four 10A or 15A Blade Fuses on each 5m injection leg.
  Wiring: 3-core cable for 5V power to end of LED strip and ground circuit. Note mapping: Brown = 5V, Blue = GND, Green/Yellow = GND (doubled up).
  Microcontroller: ESP32-S3 (Powered via 5V/GND pins).
  Logic Level Shifter: Adafruit 757 (BSS138).
  Low Side (LV): 3.3V (from ESP32 3V3 pin).
  High Side (HV): 5V (from 60A PSU).
  Data Resistors: 330Ω. Place in series between the Level Shifter output and the start of the LED data lines.
  Smoothing Capacitors: 1000µF, 10V Electrolytic. Place at each of the four main power injection points.

custom parts:
  ESP32-S3 zero: ESP32-S3 Mini Development Board, Based on ESP32-S3FH4R2 Dual-Core Processor, 240MHz Running Frequency, 2.4GHz Wi-Fi & Bluetooth 5.
  Logic Level Converter: 5V to/from 3.3V logic level converter
  WS2812 RGB LED strip: WS2812 strip
